# Fritzing sketch Assignment1IOTok (saved by Fritzing 0.9.3b)
breadboards: 1

parts:
  U1 = NodeMCU V1.0
  Mod2 = KY-011 Two Color LED Module [package="Breakout board"]
  R2 = Resistor [tolerance=±5% resistance=200 package=THT]
  R3 = Resistor [tolerance=±5% resistance=200 package=THT]
  Mod3 = KY-012 Active Buzzer Module [package="Breakout board"]
  Mod4 = KY-004 Key Switch Module [package="Breakout board"]
  R5 = Resistor [tolerance=±5% resistance=100 package=THT]
  Mod5 = KY-010 Photo Interrupter Module [package="Breakout board"]
  Componente1 = LCD1602-I2C
  Mod6 = KY-013 Analog Temperature Sensor Module [package="Breakout board"]

nets:
  N1: U1.D1, Componente1.SCL
  N2: U1.D2, Componente1.SDA
  N3: U1.D3, Mod4.S
  N4: U1.D4, Mod3.-
  VIN: U1.3V3, R5.Pin_0, Mod5.Vin, Mod6.Vin
  N5: U1.GND, Mod2.-, Mod4.-, Mod5.-, Mod6.-
  N6: U1.D5, Mod5.S
  N7: U1.D6, R2.Pin_1
  N8: U1.D7, R3.Pin_1
  N9: U1.A0, Mod6.S
  N10: Mod2.Vin, R3.Pin_0
  N11: Mod2.S, R2.Pin_0
  N12: Mod3.S, R5.Pin_1

custom parts:
  NodeMCU V1.0: ESP8266 based NodeMCU
  KY-011 Two Color LED Module: KY-011 Two Color LED Module consist of a common cathode 3mm red/green LED.
  KY-012 Active Buzzer Module: Active Piezoelectric Buzzer Module KY-012, it produces single-tone sound when signal is high. (Special thanks to vanepp for fixing the PCB holes and other errors)
  KY-004 Key Switch Module: Arduino Key Switch Module Keyes KY-004 is a push button that will output a high signal when pressed.
  KY-010 Photo Interrupter Module: KY-010 Photo Interrupter Module, it will trigger a signal when light between the sensor's gap is blocked.
  LCD1602-I2C: A standard character display, usually with 2x16 characters. Comes in many colors with LCM1602 IIC attached.
  KY-013 Analog Temperature Sensor Module: KY-013 Analog Temperature Sensor module, measures ambient temperature based on resistance of the thermistor.
